# Fritzing sketch Untitled Sketch (saved by Fritzing 1.0.2b)
breadboards: 1

parts:
  J1 = Basic Servo
  R1 = Resistor [tolerance=±5% power=0.25W resistance=220 package=THT]
  R2 = Resistor [tolerance=±5% power=0.25W resistance=220 package=THT]
  R3 = Resistor [tolerance=±5% power=0.25W resistance=220 package=THT]
  LED1 = LED - 5mm [color="Blue (430nm)" current=0.030A package="5 mm [THT]"]
  LED2 = LED - 5mm [color="Red (633nm)" current=0.030A package="5 mm [THT]"]
  LED3 = LED - 5mm [color="Infrared (850nm)" current=0.030A package="5 mm [THT]"]
  Part1 = Arduino Nano (Rev3.0)
  S1 = Pushbutton [package="[SMD]"]
  R4 = Rotary Potentiometer (Large) [maximum_resistance=10kΩ knob_status=50% power=0.5W package=THT]

nets:
  GND: J1.gnd, LED1.cathode, LED2.cathode, LED3.cathode, Part1.GND, S1.Pin_3, S1.Pin_4, R4.leg1
  VCC: J1.vcc, Part1.5V, R4.leg2
  N1: J1.pulse, Part1.D9
  N2: R1.Pin_0, LED2.anode
  N3: R1.Pin_1, Part1.D3
  N4: R2.Pin_0, LED3.anode
  N5: R2.Pin_1, Part1.D5
  N6: R3.Pin_0, LED1.anode
  N7: R3.Pin_1, Part1.D6
  N8: Part1.D4, S1.Pin_1, S1.Pin_2
  N9: Part1.A0, R4.wiper
